// Digital circuit jtag_bsr.dig as structural Verilog
module jtag_bsr (
  input  SI,
  input  ShiftDR,
  input  ClockDR,
  input  UpdateDR,
  input  Mode,
  input  PI0,
  input  PI1,
  input  PI2,
  input  PI3,
  output PO0,
  output SO,
  output PO1,
  output PO2,
  output PO3
);

  wire d_ff_2_q, d_ff_3_q, d_ff_4_q, d_ff_5_q, d_ff_6_q, d_ff_7_q, d_ff_8_q, multiplexer_1_out,
       multiplexer_2_out, multiplexer_3_out, multiplexer_4_out;

  Multiplexer multiplexer_1 (.sel(ShiftDR), .in_0(PI3), .in_1(d_ff_2_q), .out(multiplexer_1_out));
  Multiplexer multiplexer_2 (.sel(ShiftDR), .in_0(PI2), .in_1(d_ff_3_q), .out(multiplexer_2_out));
  Multiplexer multiplexer_3 (.sel(ShiftDR), .in_0(PI1), .in_1(PI0), .out(multiplexer_3_out));
  Multiplexer multiplexer_4 (.sel(ShiftDR), .in_0(PI0), .in_1(SI), .out(multiplexer_4_out));
  D_FF d_ff_1 (.D(multiplexer_1_out), .C(ClockDR), .Q(SO));  // open: nQ
  D_FF d_ff_2 (.D(multiplexer_2_out), .C(ClockDR), .Q(d_ff_2_q));  // open: nQ
  D_FF d_ff_3 (.D(multiplexer_3_out), .C(ClockDR), .Q(d_ff_3_q));  // open: nQ
  D_FF d_ff_4 (.D(multiplexer_4_out), .C(ClockDR), .Q(d_ff_4_q));  // open: nQ
  D_FF d_ff_5 (.D(SO), .C(UpdateDR), .Q(d_ff_5_q));  // open: nQ
  D_FF d_ff_6 (.D(d_ff_2_q), .C(UpdateDR), .Q(d_ff_6_q));  // open: nQ
  D_FF d_ff_7 (.D(d_ff_3_q), .C(UpdateDR), .Q(d_ff_7_q));  // open: nQ
  D_FF d_ff_8 (.D(d_ff_4_q), .C(UpdateDR), .Q(d_ff_8_q));  // open: nQ
  Multiplexer multiplexer_5 (.sel(Mode), .in_0(PI3), .in_1(d_ff_5_q), .out(PO3));
  Multiplexer multiplexer_6 (.sel(Mode), .in_0(PI2), .in_1(d_ff_6_q), .out(PO2));
  Multiplexer multiplexer_7 (.sel(Mode), .in_0(PI1), .in_1(d_ff_7_q), .out(PO1));
  Multiplexer multiplexer_8 (.sel(Mode), .in_0(PI0), .in_1(d_ff_8_q), .out(PO0));
endmodule
